# Fritzing sketch LevelAmps (saved by Fritzing 0.9.3b)
breadboards: 1

parts:
  U1 = LM124-324 Quad Opamp [package="DIP (Dual Inline)"]
  R1 = Resistor [tolerance=±5% resistance=10k package=THT]
  R2 = Resistor [tolerance=±5% resistance=10k package=THT]
  R3 = Vertical Resistor [tolerance=±5% resistance=150 package=THT]
  R4 = Vertical Resistor [tolerance=±5% resistance=150 package=THT]
  R5 = Vertical Resistor [tolerance=±5% resistance=2.2k package=THT]
  R6 = Vertical Resistor [tolerance=±5% resistance=2.2k package=THT]
  R7 = Vertical Resistor [tolerance=±5% resistance=10k package=THT]
  R8 = Vertical Resistor [tolerance=±5% resistance=10k package=THT]
  C1 = Electrolytic Capacitor top view [capacitance=1µF package="100 mil [THT, electrolytic]"]
  C2 = Electrolytic Capacitor top view [capacitance=1µF package="100 mil [THT, electrolytic]"]
  U3 = Voltage Regulator - Variable [part_number=LM317 package="TO220 [THT]"]
  R9 = Vertical Resistor [tolerance=±5% resistance=120 package=THT]
  R10 = Vertical Resistor [tolerance=±5% resistance=120 package=THT]
  U4 = Voltage Regulator - Variable [part_number=LM337 package="TO220 [THT]"]
  R11 = Vertical Resistor [tolerance=±5% resistance=680 package=THT]
  R12 = Vertical Resistor [tolerance=±5% resistance=680 package=THT]
  JP3 = Header 3 [package=molex-1x3_lock]
  JP4 = Header 3 [package=molex-1x3_lock]
  J4 = female pin header, 5 pins [form="♀ (female)"]
  Power_plug1 = Power plug
  JP5 = Header 2 [package=molex-1x2_lock]
  JP7 = Header 2 [package=molex-1x2_lock]
  C6 = Electrolytic Capacitor [capacitance=4.7µF package="100 mil [THT, electrolytic]"]
  C7 = Electrolytic Capacitor [capacitance=4.7µF package="100 mil [THT, electrolytic]"]
  J5 = Screw terminal - 2 pins [package=THT]
  J6 = Screw terminal - 2 pins [package=THT]
  D2 = Upright Rectifier Diode [part_number=1N916 package="100 mil [THT]"]
  D3 = Upright Rectifier Diode [part_number=1N916 package="100 mil [THT]"]
  D4 = Upright Rectifier Diode [part_number=1N916 package="100 mil [THT]"]
  D5 = Upright Rectifier Diode [part_number=1N916 package="100 mil [THT]"]
  D1 = Upright Rectifier Diode [part_number=1N4001 package="100 mil [THT]"]

nets:
  N1: U1.1OUT, D3.cathode, D5.anode
  N2: U1.1IN-, R1.Pin_1, R7.Pin_0, D3.anode
  0V: U1.1IN+, U1.2IN+, U1.3IN+, U1.4IN+, C1.+, C2.-, R11.Pin_1, R12.Pin_1, JP3.3, JP4.3, J4.pin2, J4.pin4, Power_plug1.GND, JP5.2, JP7.2, C6.+, C7.-
  9V: U1.VCC+, C2.+, U3.OUT, R10.Pin_1
  N3: U1.2IN-, R3.Pin_1, R5.Pin_1, J6.pin1
  N4: U1.2OUT, R1.Pin_0, R3.Pin_0
  N5: U1.3OUT, R2.Pin_0, R4.Pin_0
  N6: U1.3IN-, R4.Pin_1, R6.Pin_1, J5.pin2
  -9V: U1.VCC-, R5.Pin_0, R6.Pin_0, C1.-, R9.Pin_1, U4.IN
  N7: U1.4IN-, R2.Pin_1, R8.Pin_0, D2.anode
  N8: U1.4OUT, D2.cathode, D4.anode
  N9: R7.Pin_1, JP3.1, D5.cathode
  N10: R8.Pin_1, JP4.1, D4.cathode
  N11: U3.ADJ, R10.Pin_0, R11.Pin_0
  12V: U3.IN, J4.pin3, JP7.1, C7.+, J5.pin1, J6.pin2
  N12: R9.Pin_0, U4.ADJ, R12.Pin_0
  -12V: U4.OUT, J4.pin1, C6.-
  N13: JP3.2, D1.cathode
  N14: J4.pin5, Power_plug1.VCC
  5V: JP5.1, D1.anode

custom parts:
  Vertical Resistor: A generic resistor (0.25W)
  Vertical Resistor: A generic resistor (0.25W)
  Electrolytic Capacitor top view: A small electrolytic capacitor breadboard top view for use on perf board
  Vertical Resistor: A generic resistor (0.25W)
  Upright Rectifier Diode: A standard rectifier diode Based on Brendan Howell's work
