# Fritzing sketch SMRTYComparator (saved by Fritzing 0.9.3b)
breadboards: 1

parts:
  Q4 = TRANSISTOR_NPN [package=to-92-ammo]
  Q5 = TRANSISTOR_NPN [package=to-92-ammo]
  R1 = Vertical Resistor [tolerance=±5% resistance=9k part_number=15k||22k package=THT]
  R2 = Vertical Resistor [tolerance=±5% resistance=100k package=THT]
  R3 = Vertical Resistor [tolerance=±5% resistance=15k package=THT]
  R4 = Trimmer Potentiometer [maximum_resistance=22kΩ part_number=22k package=THT]
  JP1 = Header 3 [package=molex-1x3_lock]
  JP4 = Header 3 [package=screwterminal-3.5mm-3_lock.007s]

nets:
  N1: Q4.E, Q5.E, R1.Pin_1
  N2: Q4.B, JP4.3
  3.3V: Q4.C, R2.Pin_1, R4.leg2, JP1.3, JP4.1
  N3: Q5.B, R4.wiper
  N4: Q5.C, R2.Pin_0, JP1.1
  GND: R1.Pin_0, R3.Pin_0, JP1.2, JP4.2
  N5: R3.Pin_1, R4.leg1

custom parts:
  Vertical Resistor: A generic resistor (0.25W)
