# Fritzing sketch SMRTYSnitch2 (saved by Fritzing 0.9.3b)
circuit board: 6.84389cm x 3.60773cm
breadboards: 1

parts:
  U2 = LM124-324 Quad Opamp [part_number=TL084 package="DIP (Dual Inline)"]
  D1 = Rectifier Diode [part_number=1N4001 package="300 mil [THT]"]
  J1 = Screw terminal - 2 pins [package=THT]
  C4 = Ceramic Capacitor [capacitance=22nF voltage=50V package="100 mil [THT, multilayer]"]
  C1 = Electrolytic Capacitor [capacitance=100µF voltage=50V package="100 mil [THT, electrolytic]"]
  R3 = Resistor [tolerance=±5% resistance=1.5k package=THT]
  C2 = Electrolytic Capacitor [capacitance=1µF voltage=50V package="100 mil [THT, electrolytic]"]
  R6 = Resistor [tolerance=±5% resistance=1k package=THT]
  R7 = Resistor [tolerance=±5% resistance=4.7k package=THT]
  R4 = Resistor [tolerance=±5% resistance=100k package=THT]
  C5 = Ceramic Capacitor [capacitance=820pF voltage=50V package="100 mil [THT, multilayer]"]
  C6 = Ceramic Capacitor [capacitance=820pF voltage=50V package="100 mil [THT, multilayer]"]
  R11 = Resistor [tolerance=±5% resistance=100k package=THT]
  R12 = Resistor [tolerance=±5% resistance=1.5k package=THT]
  U3 = Optocoupler [part_number=H11A1Z package=THT]
  C3 = Ceramic Capacitor [capacitance=0.1µF voltage=50V package="100 mil [THT, multilayer]"]
  J2 = screw terminal, 3 pins
  R2 = Vertical Resistor [tolerance=±5% resistance=120 package=THT]
  R1 = Vertical Resistor [tolerance=±5% resistance=10 package=THT]
  R5 = Vertical Resistor [tolerance=±5% resistance=100k package=THT]
  R10 = Vertical Resistor [tolerance=±5% resistance=330k package=THT]
  R9 = Vertical Resistor [tolerance=±5% resistance=22k package=THT]
  R12_2 = Vertical Resistor [tolerance=±5% resistance=150k package=THT]
  R13 = Vertical Resistor [tolerance=±5% resistance=1.5k package=THT]
  L1 = Inductor [inductance=3.3mH package="400 mil [THT]"]
  U1 = TO 220 [part_number=LM317 package=TO-220]
  R9_2 = Resistor [tolerance=±5% resistance=22k package=THT]
  R14 = Resistor [tolerance=±5% resistance=100 package=THT]
  R15 = Resistor [tolerance=±5% resistance=10k package=THT]
  C7 = Ceramic Capacitor [capacitance=10nF voltage=50V package="100 mil [THT, multilayer]"]
  C8 = Electrolytic Capacitor [capacitance=1µF package="100 mil [THT, electrolytic]"]
  R17 = Vertical Resistor [tolerance=±5% resistance=100 package=THT]

nets:
  N1: U2.1OUT, U2.1IN-, R17.Pin_1
  N2: U2.1IN+, U2.3OUT, R14.Pin_0, C7.0
  17V: U2.VCC+, C2.+, R4.Pin_0, C3.1, R2.Pin_0, U1.2
  N3: U2.2IN+, R9_2.Pin_1
  N4: U2.2IN-, C5.1, R9.Pin_0
  N5: U2.2OUT, U2.4IN-, C6.1, R9.Pin_1
  N6: U2.3IN-, R15.Pin_0, C7.1
  Vref: U2.3IN+, R4.Pin_1, R5.Pin_0
  GND: U2.VCC-, J1.pin2, C1.-, R3.Pin_0, C2.-, U3.Pin_2, C3.0, R5.Pin_1, C8.-
  N7: U2.4IN+, R11.Pin_0, R10.Pin_1
  N8: U2.4OUT, R12.Pin_0, R10.Pin_0
  N9: D1.cathode, C1.+, U1.3
  N10: D1.anode, R1.Pin_0
  N11: J1.pin1, R1.Pin_1, L1.pin_0
  N12: C4.0, R6.Pin_0, R7.Pin_0
  N13: C4.1, L1.pin_1
  N14: R3.Pin_1, R2.Pin_1, U1.1
  VGND: R6.Pin_1, R11.Pin_1, R9_2.Pin_0, R14.Pin_1, R15.Pin_1, C8.+, R17.Pin_0
  N15: R7.Pin_1, C5.0, C6.0
  N16: R12.Pin_1, U3.Pin_1
  N17: U3.Pin_4, J2.pin3, R12_2.Pin_1
  N18: U3.Pin_5, J2.pin1, R13.Pin_1
  N19: U3.Pin_6, R12_2.Pin_0
  N20: J2.pin2, R13.Pin_0

custom parts:
  Vertical Resistor: A generic resistor (0.25W)
  TO 220: Standard Breadboard view modified for top view
