# Fritzing sketch SMRTYSnitch3 (saved by Fritzing 0.9.3b)
breadboards: 1

parts:
  R12 = Resistor [tolerance=±5% resistance=1.5k package=THT]
  C5 = Ceramic Capacitor [capacitance=820pF voltage=50V package="100 mil [THT, multilayer]"]
  R9 = Resistor [tolerance=±5% resistance=22k package=THT]
  C8 = Electrolytic Capacitor [capacitance=1µF package="100 mil [THT, electrolytic]"]
  R4 = Resistor [tolerance=±5% resistance=100k package=THT]
  C7 = Ceramic Capacitor [capacitance=10nF voltage=50V package="100 mil [THT, multilayer]"]
  R14 = Resistor [tolerance=±5% resistance=100 package=THT]
  R12_2 = Vertical Resistor [tolerance=±5% resistance=1k package=THT]
  J2 = screw terminal, 3 pins
  D1 = Rectifier Diode [part_number=1N4001 package="300 mil [THT]"]
  C2 = Electrolytic Capacitor [capacitance=1µF voltage=50V package="100 mil [THT, electrolytic]"]
  C1 = Electrolytic Capacitor [capacitance=100µF voltage=50V package="100 mil [THT, electrolytic]"]
  L1 = Inductor [inductance=3.3mH package="400 mil [THT]"]
  R6 = Resistor [tolerance=±5% resistance=1k package=THT]
  J1 = Screw terminal - 2 pins [package=THT]
  R3 = Resistor [tolerance=±5% resistance=1.5k package=THT]
  R15 = Resistor [tolerance=±5% resistance=10k package=THT]
  U1 = TO 220 [part_number=LM317 package=TO-220]
  C3 = Ceramic Capacitor [capacitance=0.1µF voltage=50V package="100 mil [THT, multilayer]"]
  R7 = Resistor [tolerance=±5% resistance=4.7k package=THT]
  C6 = Ceramic Capacitor [capacitance=820pF voltage=50V package="100 mil [THT, multilayer]"]
  R1 = Vertical Resistor [tolerance=±5% resistance=100 package=THT]
  R5 = Vertical Resistor [tolerance=±5% resistance=100k package=THT]
  R13 = Vertical Resistor [tolerance=±5% resistance=330k package=THT]
  U2 = LM124-324 Quad Opamp [part_number=TL084 package="DIP (Dual Inline)"]
  R9_2 = Vertical Resistor [tolerance=±5% resistance=22k package=THT]
  R2 = Vertical Resistor [tolerance=±5% resistance=120 package=THT]
  U3 = Optocoupler [part_number=H11A1Z package=THT]
  R11 = Resistor [tolerance=±5% resistance=100k package=THT]
  C4 = Ceramic Capacitor [capacitance=22nF voltage=50V package="100 mil [THT, multilayer]"]
  R16 = Vertical Resistor [tolerance=±5% resistance=1.5k package=THT]
  C9 = Ceramic Capacitor [capacitance=10nF package="0805 [SMD, multilayer]"]
  U4 = Quad Comparator [part_number=LM239 package="DIP (Dual Inline) [THT]"]
  Part1 = Quad Comparator [part_number=LM339 package="DIP (Dual Inline) [THT]"]
  U4_1 = Quad Comparator [part_number=LM239 package="DIP (Dual Inline) [THT]"]
  U4_2 = Quad Comparator [part_number=LM239 package="DIP (Dual Inline) [THT]"]
  U4_3 = Quad Comparator [part_number=LM239 package="DIP (Dual Inline) [THT]"]
  U4_4 = Quad Comparator [part_number=LM239 package="DIP (Dual Inline) [THT]"]
  R19 = Vertical Resistor [tolerance=±5% resistance=220k package=THT]
  R20 = Vertical Resistor [tolerance=±5% resistance=7.7k part_number="(10k || 33k)" package=THT]
  C10 = Ceramic Capacitor [capacitance=47pF package="0805 [SMD, multilayer]"]

nets:
  N1: R12.Pin_0, U3.Pin_1
  17V: R12.Pin_1, R4.Pin_0, C2.+, U1.2, C3.1, U2.VCC+, R2.Pin_0, U4.connector2, Part1.pin_3
  N2: C5.0, R7.Pin_1, C6.0
  N3: C5.1, U2.2IN-, R9_2.Pin_0
  VGND: R9.Pin_0, C8.+, R14.Pin_1, R6.Pin_1, R15.Pin_1, R11.Pin_1, R16.Pin_0, U4.connector5, U4_1.pin_6
  N4: R9.Pin_1, U2.2IN+
  GND: C8.-, C2.-, C1.-, J1.pin2, R3.Pin_0, C3.0, R5.Pin_1, U2.VCC-, U4.connector1, U4.connector3, U4.connector4, U4.connector7, U4.connector8, U4.connector9, U4.connector10, U4.connector11, U4.connector12, U4.connector13, Part1.pin_12, U4_2.pin_2, U4_2.pin_4, U4_2.pin_5, U4_3.pin_8, U4_3.pin_9, U4_3.pin_14, U4_4.pin_10, U4_4.pin_13
  Vref: R4.Pin_1, R5.Pin_0, U2.3IN+
  N5: C7.0, R14.Pin_0, U2.3OUT
  N6: C7.1, R15.Pin_0, U2.3IN-
  N7: R12_2.Pin_0, U3.Pin_6
  N8: R12_2.Pin_1, J2.pin3, U3.Pin_4
  N9: J2.pin1, R13.Pin_1, U3.Pin_5
  N10: J2.pin2, R13.Pin_0
  N11: D1.cathode, C1.+, U1.3
  N12: D1.anode, R1.Pin_0
  N13: L1.pin_0, J1.pin1, R1.Pin_1
  N14: L1.pin_1, C4.1
  N15: R6.Pin_0, R7.Pin_0, C4.0
  N16: R3.Pin_1, U1.1, R2.Pin_1
  N17: C6.1, U2.2OUT, R9_2.Pin_1, C9.1
  N18: U2.1OUT, U2.1IN-, R20.Pin_0
  Signal: U2.1IN+, R16.Pin_1, C9.0
  N19: U2.4IN+, R11.Pin_0
  N20: U2.4IN-, U2.4OUT
  N21: U3.Pin_2, U4.connector0, U4_1.pin_1, R19.Pin_0, C10.0
  N22: U3.Pin_3, U4.connector6, U4_1.pin_7, R19.Pin_1, R20.Pin_1, C10.1

notes:
  not really
  speed up

custom parts:
  Vertical Resistor: A generic resistor (0.25W)
  TO 220: Standard Breadboard view modified for top view
  Vertical Resistor: A generic resistor (0.25W)
  Quad Comparator: LM239 Quad Comparator
  Quad Comparator: LM239 Quad Comparator
  Quad Comparator: LM239 Quad Comparator
  Quad Comparator: LM239 Quad Comparator
  Quad Comparator: LM239 Quad Comparator
